# Fritzing sketch perler_tool (saved by Fritzing 0.9.3b)
breadboards: 1

parts:
  Raspberry_Pi_1 = Raspberry Pi 3 [part_number=RPI-3-V1.2]
  IC2 = MCP3008 8-channel 10-bit ADC [part_number=MCP3008]
  R1 = Resistor [tolerance=±5% resistance=220 package="2010 [SMD]"]
  R2 = Resistor [tolerance=±5% resistance=220 package="2010 [SMD]"]
  CameraLight = LEDs [package=led10mm]
  R4 = Resistor [tolerance=±5% resistance=220 package="2010 [SMD]"]
  J1 = Basic Servo
  M1 = DC Motor
  Mosfet_driver_module1 = IFR520 MOS module [package=THT]
  External_5v = 2.1mm Barrel Jack with Terminal Block

nets:
  N1: Raspberry_Pi_1.GPIO23, J1.pulse
  N2: Raspberry_Pi_1.GPIO15, Mosfet_driver_module1.pin1
  N3: Raspberry_Pi_1.GND, IC2.no_name_yet#9, IC2.no_name_yet#14, CameraLight.A, Mosfet_driver_module1.pin3
  N4: Raspberry_Pi_1.5V, IC2.no_name_yet#15, IC2.no_name_yet#16, Mosfet_driver_module1.pin2
  N5: IC2.no_name_yet#4, R4.Pin_0
  N6: R1.Pin_0, CameraLight.C
  N7: R1.Pin_1, R2.Pin_1, J1.vcc, Mosfet_driver_module1.pin6, External_5v.POS
  N8: J1.gnd, Mosfet_driver_module1.pin7, External_5v.NEG
  N9: M1.pin_1, Mosfet_driver_module1.pin4
  N10: M1.pin_2, Mosfet_driver_module1.pin5

custom parts:
  IFR520 MOS module: Breakout board for the IFR520 MOSFET transistor. The module is designed to switch heavy DC loads from a single digital pin of your microcontroller. Its main purpose is to provide a low cost way to drive a DC motor for robotics applications, but the module can be used to control most high current DC loads. Screw terminals are provided to interface to your load and external power source. An LED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
